// Logisim project 8BCPU.circ as structural Verilog: 5 circuits, main circuit main
module main (
  input  [7:0] Testing_Data,
  input  WE,
  input  OE_Testing_Data,
  input  OE,
  input  Counter_OE,
  input  Internal_OE,
  input  Counter_Enable,
  input  WE_2,
  input  OE_2,
  input  WE_3,
  input  OE_3,
  input  WE_4,
  input  WE_5,
  input  OE_4,
  input  OE_5,
  input  WE_6,
  output [3:0] MAR_Content,
  output [3:0] Counter_Content,
  output [7:0] IR_Content,
  output [7:0] MBR_Content,
  output [7:0] Reg_A_Content,
  output [7:0] ALU_Result,
  output [7:0] out_23,
  output [7:0] Reg_B_Content
);

  wire CLK_out;
  wire [3:0] controlled_buffer_1_out, MAR_dout;
  wire [7:0] ALU_dout, Instruction_Register_dout;

  Clock CLK (.out(CLK_out));
  Counter #(.width(4), .max('h3)) Program_Counter (
    .D(controlled_buffer_1_out), .count(Counter_Enable), .Q(Counter_Content), .clk(CLK_out));  // open: load, carry, clr
  Register Instruction_Register (
    .CLK(CLK_out), .WE(WE_3), .OE(OE_3), .Din(ALU_dout), .Dout(Instruction_Register_dout),
    .Stored_Data(IR_Content));
  Register Register_A (.CLK(CLK_out), .WE(WE_4), .Din(ALU_dout), .Stored_Data(Reg_A_Content));  // open: OE, Dout
  ALU ALU (
    .Reg_A(Reg_A_Content), .Reg_B(Reg_B_Content), .OE(OE_5), .ALU_Result(ALU_Result), .Dout(ALU_dout));  // open: Carry_Output
  Register Register_B (.CLK(CLK_out), .WE(WE_6), .Din(ALU_dout), .Stored_Data(Reg_B_Content));  // open: OE, Dout
  assign controlled_buffer_1_out = Counter_OE ? Counter_Content : 4'bz;  // Controlled_Buffer controlled_buffer_1
  BitSelector #(.group(4)) bitselector_1 (.in(Instruction_Register_dout), .out(controlled_buffer_1_out), .sel(1'b0));
  assign ALU_dout = OE_Testing_Data ? Testing_Data : 8'bz;  // Controlled_Buffer controlled_buffer_2
  LED D7 (.in(ALU_dout[7]));
  LED D6 (.in(ALU_dout[6]));
  LED D4 (.in(ALU_dout[4]));
  LED D3 (.in(ALU_dout[3]));
  LED D2 (.in(ALU_dout[2]));
  LED D5 (.in(ALU_dout[5]));
  LED D0 (.in(ALU_dout[0]));
  LED D1 (.in(ALU_dout[1]));
  MAR MAR (.CLK(CLK_out), .WE(WE), .OE(OE), .Din(controlled_buffer_1_out), .Dout(MAR_dout), .Stored_Data(MAR_Content));
  assign ALU_dout = Internal_OE ? MBR_Content : 8'bz;  // Controlled_Buffer controlled_buffer_3
  Register MBR (.CLK(CLK_out), .WE(WE_2), .OE(OE_2), .Din(ALU_dout), .Dout(ALU_dout), .Stored_Data(MBR_Content));
  Register Output_Register (.CLK(CLK_out), .WE(WE_5), .OE(OE_4), .Din(ALU_dout), .Dout(ALU_dout), .Stored_Data(out_23));
  LED D7_2 (.in(ALU_dout[7]));
  LED D6_2 (.in(ALU_dout[6]));
  LED D5_2 (.in(ALU_dout[5]));
  LED D2_2 (.in(ALU_dout[2]));
  LED D3_2 (.in(ALU_dout[3]));
  LED D4_2 (.in(ALU_dout[4]));
  LED D1_2 (.in(ALU_dout[1]));
  LED D0_2 (.in(ALU_dout[0]));

  // Notes on the sheet:
  //   Internal Address Bus (4 bits)
  //   Internal Data Bus
  //   External Address Bus
  //   External Data Bus
endmodule

module Memory (
  input  CLK,
  input  WE,
  input  Din,
  input  OE,
  input  RESET,
  output Dout,
  output Stored_Data
);

  wire and_1_out, and_2_out, not_1_out, or_1_out;

  not not_1 (not_1_out, WE);
  and and_1 (and_1_out, Stored_Data, not_1_out);
  and and_2 (and_2_out, WE, Din);
  or or_1 (or_1_out, and_1_out, and_2_out);
  D_Flip_Flop d_ff_1 (.clk(CLK), .D(or_1_out), .Q(Stored_Data), .reset(RESET));  // open: Qn, preset, en
  assign Dout = OE ? Stored_Data : 1'bz;  // Controlled_Buffer controlled_buffer_1

  // Notes on the sheet:
  //   Memory Cell
endmodule

module Register (
  input  CLK,
  input  WE,
  input  OE,
  input  [7:0] Din,
  output [7:0] Dout,
  output [7:0] Stored_Data
);

  Memory _0 (.CLK(CLK), .WE(WE), .Din(Din[0]), .OE(OE), .Dout(Dout[0]), .Stored_Data(Stored_Data[0]));  // open: RESET
  Memory _1 (.CLK(CLK), .WE(WE), .Din(Din[1]), .OE(OE), .Dout(Dout[1]), .Stored_Data(Stored_Data[1]));  // open: RESET
  Memory _2 (.CLK(CLK), .WE(WE), .Din(Din[2]), .OE(OE), .Dout(Dout[2]), .Stored_Data(Stored_Data[2]));  // open: RESET
  Memory _3 (.CLK(CLK), .WE(WE), .Din(Din[3]), .OE(OE), .Dout(Dout[3]), .Stored_Data(Stored_Data[3]));  // open: RESET
  Memory _4 (.CLK(CLK), .WE(WE), .Din(Din[4]), .OE(OE), .Dout(Dout[4]), .Stored_Data(Stored_Data[4]));  // open: RESET
  Memory _5 (.CLK(CLK), .WE(WE), .Din(Din[5]), .OE(OE), .Dout(Dout[5]), .Stored_Data(Stored_Data[5]));  // open: RESET
  Memory _6 (.CLK(CLK), .WE(WE), .Din(Din[6]), .OE(OE), .Dout(Dout[6]), .Stored_Data(Stored_Data[6]));  // open: RESET
  Memory _7 (.CLK(CLK), .WE(WE), .Din(Din[7]), .OE(OE), .Dout(Dout[7]), .Stored_Data(Stored_Data[7]));  // open: RESET

  // Notes on the sheet:
  //   Memory Register
endmodule

module MAR (
  input  CLK,
  input  WE,
  input  OE,
  input  [3:0] Din,
  output [3:0] Dout,
  output [3:0] Stored_Data
);

  Memory _0 (.CLK(CLK), .WE(WE), .Din(Din[0]), .OE(OE), .Dout(Dout[0]), .Stored_Data(Stored_Data[0]));  // open: RESET
  Memory _1 (.CLK(CLK), .WE(WE), .Din(Din[1]), .OE(OE), .Dout(Dout[1]), .Stored_Data(Stored_Data[1]));  // open: RESET
  Memory _2 (.CLK(CLK), .WE(WE), .Din(Din[2]), .OE(OE), .Dout(Dout[2]), .Stored_Data(Stored_Data[2]));  // open: RESET
  Memory _3 (.CLK(CLK), .WE(WE), .Din(Din[3]), .OE(OE), .Dout(Dout[3]), .Stored_Data(Stored_Data[3]));  // open: RESET

  // Notes on the sheet:
  //   MAR
endmodule

module ALU (
  input  [7:0] Reg_A,
  input  [7:0] Reg_B,
  input  OE,
  output [7:0] ALU_Result,
  output [7:0] Dout,
  output Carry_Output
);

  Adder adder_1 (.a(Reg_A), .b(Reg_B), .out(ALU_Result), .cout(Carry_Output));  // open: cin
  assign Dout = OE ? ALU_Result : 8'bz;  // Controlled_Buffer controlled_buffer_1

  // Notes on the sheet:
  //   ALU (8 bits)
endmodule
